// Logisim project MemoriaDados.circ as structural Verilog: 1 circuit, main circuit main
module main (
  input  [31:0] DW,
  input  [4:0] ADDR,
  input  WE,
  input  CKL,
  output [31:0] DR
);

  wire not_1_out;

  not not_1 (not_1_out, WE);
  RAM #(.addrWidth(5)) ram_1 (.addr(ADDR), .we(WE), .oe(not_1_out), .clk(CKL), .din(DW[31:24]), .dout(DR[31:24]));
  RAM #(.addrWidth(5)) ram_2 (.addr(ADDR), .we(WE), .oe(not_1_out), .clk(CKL), .din(DW[23:16]), .dout(DR[23:16]));
  RAM #(.addrWidth(5)) ram_3 (.addr(ADDR), .we(WE), .oe(not_1_out), .clk(CKL), .din(DW[15:8]), .dout(DR[15:8]));
  RAM #(.addrWidth(5)) ram_4 (.addr(ADDR), .we(WE), .oe(not_1_out), .clk(CKL), .din(DW[7:0]), .dout(DR[7:0]));
endmodule
